# Fritzing sketch Car_bt (saved by Fritzing 0.9.9b)
breadboards: 1

parts:
  Parça2 = Arduino Uno (Rev3)
  R1 = Resistor [tolerance=±5% resistance=1000 package="0402 [SMD]"]
  R2 = Resistor [tolerance=±5% resistance=1000 package="0402 [SMD]"]
  R3 = Resistor [tolerance=±5% resistance=1000 package="0402 [SMD]"]
  BT1 = Bluetooth HC-06u [package=THT]
  L298N1 = L298N DC motor driver
  M2 = DC Motor  # not connected
  VCC1 = Battery block 9V
  M3 = DC Motor  # not connected
  J1 = Piezo Speaker

nets:
  N1: Parça2.D8, R1.Pin_0
  N2: Parça2.D9_PWM, L298N1.ENB
  N3: Parça2.D10_PWM/SS, L298N1.ENA
  N4: Parça2.D11_PWM/MOSI, J1.pin2
  N5: Parça2.D12/MISO, BT1.RXD
  N6: Parça2.D4, L298N1.IN1
  N7: Parça2.D5_PWM, L298N1.IN2
  N8: Parça2.D6_PWM, L298N1.IN3
  N9: Parça2.D7, L298N1.IN4
  5V: Parça2.5V, BT1.VCC
  GND: Parça2.GND, BT1.GND, VCC1.-, J1.pin1
  N10: R1.Pin_1, R2.Pin_0, BT1.TXD
  N11: R2.Pin_1, R3.Pin_0

custom parts:
  Bluetooth HC-06u: Bluetooth HC-06 - face up, pins down 16.5mm x 37.5mm PCB
  L298N DC motor driver: 2x DC motor driver with 78M05 positive voltage regulator (7..35 V) L298N: max 46 V, 2 A Set 5 V Enable jumper to enable 5 V regultor (needed for the L298N) and +5 V output at screw terminal or supply external +5 V at screw terminal Set ENA and/or ENB to +5 V to enable motor permanently or supply ENA and/or ENB with PWM signal IN1 and IN2 set rotation directory for motor A (OUT1/OUT2) IN2 and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
